# Fritzing sketch Knocker_Mash_PID-Nano_ESP8266F-v100 (saved by Fritzing 0.9.3b)
circuit board: 4.6cm x 5.20044cm
breadboards: 1

parts:
  V_REG3_3 = Voltage Regulator - 3.3V [package="TO220 [THT]"]
  SEN1 = DS18B20 1-Wire Temperature Sensor [part_number=DS18B20]
  ARDUINO_NANO = Arduino Nano (Rev3.0)
  SEN2 = DS18B20 1-Wire Temperature Sensor [part_number=DS18B20]
  4_7kΩ = Resistor [tolerance=±5% resistance=4.7k package=THT]
  RESET = Pushbutton [part_number=RESET package="[THT]"]
  FLASH = Pushbutton [part_number=FLASH package="[THT]"]
  ESP8266-01 = ESP8266 WiFi Module [part_number=ESP8266]
  10kΩ = Resistor [tolerance=±5% resistance=10k package=THT]
  10kΩ_2 = Resistor [tolerance=±5% resistance=10k package=THT]
  SSR = female pin header, 2 pins [form="♀ (female)" part_number=SSR]
  FAN = female pin header, 2 pins [form="♀ (female)" part_number=Fan]
  LCD_16x2 = female pin header, 4 pins [form="♀ (female)" part_number="I2C LCD 16x2"]
  LEFT = Pushbutton [package="[THT]"]
  DOWN = Pushbutton [package="[THT]"]
  UP = Pushbutton [package="[THT]"]
  RIGHT = Pushbutton [package="[THT]"]
  SELECT = Pushbutton [package="[THT]"]
  TX/RX = female pin header, 2 pins [form="♀ (female)"]
  FLASHING_THE_NANO_AND_ESP = female pin header, 2 pins [form="♀ (female)"]

nets:
  VDD: V_REG3_3.input_voltage, SEN1.VDD, ARDUINO_NANO.5V, SEN2.VDD, 4_7kΩ.Pin_0, FAN.pin1, LCD_16x2.pin2
  GND: V_REG3_3.GND, SEN1.GND, ARDUINO_NANO.GND, SEN2.GND, RESET.Pin_3, RESET.Pin_4, FLASH.Pin_1, FLASH.Pin_2, ESP8266-01.GND, SSR.pin2, FAN.pin2, LCD_16x2.pin1, LEFT.Pin_3, LEFT.Pin_4, DOWN.Pin_3, DOWN.Pin_4, UP.Pin_3, UP.Pin_4, RIGHT.Pin_3, RIGHT.Pin_4, SELECT.Pin_3, SELECT.Pin_4
  N1: V_REG3_3.output_voltage, ESP8266-01.VCC, 10kΩ.Pin_0, 10kΩ_2.Pin_0
  N2: SEN1.DQ, ARDUINO_NANO.A2, SEN2.DQ, 4_7kΩ.Pin_1
  N3: ARDUINO_NANO.D1/TX, ESP8266-01.RXD, TX/RX.pin2, FLASHING_THE_NANO_AND_ESP.pin2
  N4: ARDUINO_NANO.D0/RX, ESP8266-01.TXD, TX/RX.pin1, FLASHING_THE_NANO_AND_ESP.pin1
  N5: ARDUINO_NANO.D3, LEFT.Pin_1, LEFT.Pin_2
  N6: ARDUINO_NANO.D4, RIGHT.Pin_1, RIGHT.Pin_2
  N7: ARDUINO_NANO.D5, UP.Pin_1, UP.Pin_2
  N8: ARDUINO_NANO.D6, DOWN.Pin_1, DOWN.Pin_2
  N9: ARDUINO_NANO.D7, SELECT.Pin_1, SELECT.Pin_2
  N10: ARDUINO_NANO.A5, LCD_16x2.pin3
  N11: ARDUINO_NANO.A4, LCD_16x2.pin4
  N12: ARDUINO_NANO.A1, SSR.pin1
  N13: RESET.Pin_1, RESET.Pin_2, ESP8266-01.RST, 10kΩ.Pin_1
  N14: FLASH.Pin_3, FLASH.Pin_4, ESP8266-01.GPIO_0
  N15: ESP8266-01.CH_PD, 10kΩ_2.Pin_1

notes:
  5V   GND  3.3V
  VCC
  GND
  SDA
  SCL
  +
  -
  D13
  D12
  FAN
  SSR
  FLASH
  RESET
  DOWN
  LEFT
  UP
  RIGHT
  SELECT
  I2C LCD 16x2
  GND, VCC, SCL, SDA

custom parts:
  ESP8266 WiFi Module: Generic WiFi Module based on the ESP8266 with onboard PCB antenna and UART communications
