# Fritzing sketch PID_PoM-Nano&ESP8266F-v100 (saved by Fritzing 0.9.3b)
circuit board: 4.54317cm x 4.43516cm
breadboards: 1

parts:
  Part1 = LCD1602-I2C  # not connected
  U1 = Voltage Regulator - 3.3V [package="TO220 [THT]"]
  DS1 = DS18B20 1-Wire Temperature Sensor [part_number=DS18B20]
  Part2 = Arduino Nano (Rev3.0)
  DS2 = DS18B20 1-Wire Temperature Sensor [part_number=DS18B20]
  R2 = Resistor [tolerance=±5% resistance=220 package=THT]
  S6 = Pushbutton [part_number=RESET package="[THT]"]
  S7 = Pushbutton [part_number=PROGRAM package="[THT]"]
  U5 = ESP8266 WiFi Module [part_number=ESP8266]
  R3 = Resistor [tolerance=±5% resistance=10k package=THT]
  R4 = Resistor [tolerance=±5% resistance=10k package=THT]
  J1 = female pin header, 2 pins [form="♀ (female)" part_number=SSR]
  J2 = female pin header, 2 pins [form="♀ (female)" part_number=Fan]
  J3 = female pin header, 4 pins [form="♀ (female)"]
  S3 = Pushbutton [package="[THT]"]
  S1 = Pushbutton [package="[THT]"]
  S2 = Pushbutton [package="[THT]"]
  S4 = Pushbutton [package="[THT]"]
  S5 = Pushbutton [package="[THT]"]

nets:
  VDD: U1.input_voltage, DS1.VDD, Part2.5V, DS2.VDD, R2.Pin_0, J2.pin1, J3.pin2
  GND: U1.GND, DS1.GND, Part2.GND, DS2.GND, S6.Pin_3, S6.Pin_4, S7.Pin_1, S7.Pin_2, U5.GND, J1.pin2, J2.pin2, J3.pin1, S3.Pin_3, S3.Pin_4, S1.Pin_3, S1.Pin_4, S2.Pin_3, S2.Pin_4, S4.Pin_3, S4.Pin_4, S5.Pin_3, S5.Pin_4
  N1: U1.output_voltage, U5.VCC, R3.Pin_0, R4.Pin_0
  N2: DS1.DQ, Part2.A2, DS2.DQ, R2.Pin_1
  N3: Part2.D1/TX, U5.RXD
  N4: Part2.D0/RX, U5.TXD
  N5: Part2.D3, S1.Pin_1, S1.Pin_2
  N6: Part2.D4, S4.Pin_1, S4.Pin_2
  N7: Part2.D5, S2.Pin_1, S2.Pin_2
  N8: Part2.D6, S3.Pin_1, S3.Pin_2
  N9: Part2.D7, S5.Pin_1, S5.Pin_2
  N10: Part2.A5, J3.pin3
  N11: Part2.A4, J3.pin4
  N12: Part2.A1, J1.pin1
  N13: S6.Pin_1, S6.Pin_2, U5.RST, R3.Pin_1
  N14: S7.Pin_3, S7.Pin_4, U5.GPIO_0
  N15: U5.CH_PD, R4.Pin_1

custom parts:
  LCD1602-I2C: A standard character display, usually with 2x16 characters. Comes in many colors with LCM1602 IIC attached.
  ESP8266 WiFi Module: Generic WiFi Module based on the ESP8266 with onboard PCB antenna and UART communications
